# Fritzing sketch ColorizeFritzing (saved by Fritzing 0.9.3b)
breadboards: 1

parts:
  Componente1 = Arduino Uno (Rev3)
  R1 = Resistor [tolerance=±5% resistance=220 package=THT]
  R2 = Resistor [tolerance=±5% resistance=220 package=THT]
  R3 = Resistor [tolerance=±5% resistance=220 package=THT]
  LED1 = RGB LED - (4 legs) [package="5 mm [THT]"]  # not connected
  Componente2 = Humidity Temperature Sensor SHT15
  R4 = Resistor [tolerance=±5% resistance=4.7k package=THT]
  R5 = Resistor [tolerance=±5% resistance=4.7k package=THT]
  U1 = ESP8266 WiFi Module [part_number=ESP8266]

nets:
  N1: Componente1.A4/SDA, Componente2.SDA, R4.Pin_0
  N2: Componente1.A5/SCL, Componente2.SCL, R5.Pin_0
  N3: Componente1.D9_PWM, R3.Pin_1
  N4: Componente1.D10_PWM/SS, R2.Pin_1
  N5: Componente1.D11_PWM/MOSI, R1.Pin_1
  N6: Componente1.D2, U1.TX
  N7: Componente1.D3_PWM, U1.RX
  3V3: Componente1.3V3, U1.3.3V
  5V: Componente1.5V, Componente2.VCC, R4.Pin_1, R5.Pin_1
  GND: Componente1.GND, Componente2.GND, U1.GND
